// Logisim project hamming_basic_1.circ as structural Verilog: 1 circuit, main circuit main
module main (
);

  wire dipswitch_1_p1, dipswitch_1_p2, dipswitch_1_p3, dipswitch_1_p4;

  // DipSwitch #(.number(4)) dipswitch_1: pin names not known; wires that end beside it: dipswitch_1_p1, dipswitch_1_p2, dipswitch_1_p3, dipswitch_1_p4

  // Notes on the sheet:
  //   D1
  //   D2
  //   D3
  //   D4
endmodule
